# Fritzing sketch ServoTest Sketch (saved by Fritzing 0.9.10b)
breadboards: 1

parts:
  R2 = TRIMPOT [maximum_resistance=10kΩ knob_status=50% power=0.5W package=trimpot_pth_s3_lock]
  Mod1 = Amica NodeMCU DEVKIT 1.0
  U1 = 74AHCT125 [part_number=SN74AHCT125 package=dil14]
  J1 = Basic Servo
  J2 = Basic Servo

nets:
  GND: R2.CCW, Mod1.pin2, Mod1.pin_9, Mod1.pin_25, Mod1.pin_29, U1.1OE, U1.2OE, U1.GND, J1.gnd, J2.gnd
  N1: R2.WIPER, Mod1.pin_16
  N2: R2.CW, Mod1.pin1, Mod1.pin_10, Mod1.pin_26
  N3: Mod1.pin_13, U1.2A
  N4: Mod1.pin_14, U1.1A
  VCC: Mod1.pin_30, U1.VCC, J1.vcc, J2.vcc
  N5: U1.1Y, J1.pulse
  N6: U1.2Y, J2.pulse

custom parts:
  74AHCT125: Quad Level-Shifter (3V to 5V) Quadruple Bus Buffer Gates With 3-State Outputs
